# Fritzing sketch Robot Fritzing Diagram (saved by Fritzing 0.9.6b)
breadboards: 1

parts:
  S1 = H-Bridge with L298N
  Part1 = SRF05 Ultrasonic Rangefinder
  Part2 = Arduino Uno (Rev3)
  M1 = DC Motor
  M2 = DC Motor
  J1 = Basic Servo  # not connected
  LED2 = LED - 5mm [color="Red (633nm)" current=0.030 package="5 mm [THT]"]
  LED3 = LED - 5mm [color="Green (565nm)" current=0.030 package="5 mm [THT]"]
  LED4 = LED - 5mm [color="Blue (505nm)" current=0.030 package="5 mm [THT]"]
  R1 = Resistor [tolerance=±5% resistance=100 power=0.25 package=THT]
  R2 = Resistor [tolerance=±5% resistance=100 power=0.25 package=THT]
  R3 = Resistor [tolerance=±5% resistance=180 power=0.25 package=THT]
  VCC1 = Battery
  IR1 = TSOP312.., 314.. [package=THT]

nets:
  N1: S1.12V, VCC1.+
  N2: S1.GND, VCC1.-
  N3: S1.ENA, Part2.D5_PWM
  N4: S1.IN1, Part2.D10_PWM/SS
  N5: S1.IN2, Part2.D9_PWM
  N6: S1.IN3, Part2.D4
  N7: S1.IN4, Part2.D7
  N8: S1.ENB, Part2.D6_PWM
  N9: S1.M1-01, M1.pin_2
  N10: S1.M1-02, M1.pin_1
  N11: S1.M2-01, M2.pin_1
  N12: S1.M2-02, M2.pin_2
  VCC: Part1.VCC, Part2.5V, IR1.Vs
  N13: Part1.Trig, Part2.A1
  N14: Part1.Echo, Part2.D8
  GND: Part1.GND, Part2.GND, LED2.cathode, LED3.cathode, LED4.cathode, IR1.GND
  N15: Part2.D11_PWM/MOSI, R3.Pin_1
  N16: Part2.D12/MISO, R2.Pin_1
  N17: Part2.D13/SCK, R1.Pin_1
  N18: Part2.D2, IR1.Data
  N19: LED2.anode, R3.Pin_0
  N20: LED3.anode, R2.Pin_0
  N21: LED4.anode, R1.Pin_0

custom parts:
  H-Bridge with L298N: h-bridge
